# Fritzing sketch Untitled Sketch (saved by Fritzing 0.9.4)
breadboards: 1

parts:
  Q1_2N2222 = NPN-Transistor [package="TO92 [THT]"]
  RB = Resistor [tolerance=±5% resistance=100k package=THT]
  RC = Resistor [tolerance=±5% resistance=1k package=THT]
  EB = Screw terminal - 2 pins [package=THT]
  EC = Screw terminal - 2 pins [package=THT]

nets:
  N1: Q1_2N2222.E, EB.pin1, EC.pin1
  N2: Q1_2N2222.B, RB.Pin_0
  N3: Q1_2N2222.C, RC.Pin_0
  N4: RB.Pin_1, EB.pin2
  N5: RC.Pin_1, EC.pin2
