# Fritzing sketch Untitled Sketch (saved by Fritzing 0.9.4)
breadboards: 1

parts:
  Q1 = NPN-Transistor [part_number=Q2N2222 package="TO92 [THT]"]
  RE = Resistor [tolerance=±5% resistance=1k package=THT]
  RC = Resistor [tolerance=±5% resistance=2.2k package=THT]
  EC = Screw terminal - 2 pins [package=THT]
  RB2 = Resistor [tolerance=±5% resistance=10k package=THT]
  RB1 = Resistor [tolerance=±0.05% resistance=57k package=THT]

nets:
  N1: Q1.E, RE.Pin_1
  N2: Q1.B, RB2.Pin_1, RB1.Pin_0
  N3: Q1.C, RC.Pin_0
  N4: RE.Pin_0, EC.pin1, RB2.Pin_0
  N5: RC.Pin_1, EC.pin2, RB1.Pin_1
