# Fritzing sketch Untitled Sketch (saved by Fritzing 0.9.4)
breadboards: 1

parts:
  Q1 = NPN-Transistor [part_number=Q2N2222 package="TO92 [THT]"]
  RE1 = Resistor [tolerance=±5% resistance=100 package=THT]
  RC = Resistor [tolerance=±5% resistance=2.2k package=THT]
  EC = Screw terminal - 2 pins [package=THT]
  RB2 = Resistor [tolerance=±5% resistance=10k package=THT]
  RB1 = Resistor [tolerance=±0.05% resistance=22k package=THT]
  RE2 = Resistor [tolerance=±5% resistance=900 package=THT]
  Eg = Screw terminal - 2 pins [package=THT]
  C1 = Electrolytic Capacitor [capacitance=4.7µF package="100 mil [THT, electrolytic]"]
  C2 = Electrolytic Capacitor [capacitance=4.7µF package="100 mil [THT, electrolytic]"]
  RL = Resistor [tolerance=±5% resistance=10k package=THT]
  CE = Electrolytic Capacitor [capacitance=470µF package="100 mil [THT, electrolytic]"]

nets:
  N1: Q1.E, RE1.Pin_1
  N2: Q1.B, RB2.Pin_1, RB1.Pin_0, C1.-
  N3: Q1.C, RC.Pin_0, C2.-
  N4: RE1.Pin_0, RE2.Pin_1
  N5: RC.Pin_1, EC.pin2, RB1.Pin_1
  N6: EC.pin1, RB2.Pin_0, RE2.Pin_0, Eg.pin1, RL.Pin_1, CE.+
  N7: Eg.pin2, C1.+
  N8: C2.+, RL.Pin_0
